// Logisim project finally.circ as structural Verilog: 10 circuits, main circuit main
module main (
  input  [15:0] in_1,
  input  in_2,
  input  [1:0] in_3,
  input  \RAM清空 
);

  wire \ALU_X输入选择 , \ALU_X输入选择_t , \beq相等 , \bgt大于 , \bne不相等 , \jump指令输入 , multiplexer_2_out,
       multiplexer_8_out, \n16位alu_1_p6 , \RAM存储 , \RAM存储_t , \RAM输出 , \RAM输出_t , S3, \写入寄存器数据1 , \写入寄存器数据2 ,
       \时钟 , \时钟2 , \立即数扩展方式 , \立即数扩展方式_t , \符号位 , \计数器加载端 , \计数器加载端_t , \计数器计数端 , \计数器计数端_t , \读写信号 ,
       \读写信号_t ;
  wire [1:0] \ALU_Y输入选择 , multiplexer_1_out, \读出选择1 , \读出选择2 , \选择寄存器信号 ;
  wire [2:0] func;
  wire [3:0] \ALU计算方式 , \op码 ;
  wire [11:3] \jump数 ;
  wire [15:0] \_1寄存器数据 , \_2寄存器数据 , \_3寄存器数据 , \_4寄存器数据 , bit_extender_1_out, counter_1_q, multiplexer_3_out,
       multiplexer_4_out, multiplexer_5_out, multiplexer_6_out, multiplexer_7_out, \n16位alu_1_p5 ,
       \下地址处理_1_下条指令地址 , \存储器数据 , \寄存器组_1_a输出 , \寄存器组_1_b输出 , \立即数扩展_1_扩展后的数 ;

  Clock clock_1 (.out(\时钟2 ));
  Multiplexer #(.width(2), .enable("false")) multiplexer_1 (
    .in0(\选择寄存器信号 ), .in1(in_3), .out(multiplexer_1_out), .sel(in_2));
  Multiplexer #(.enable("false")) multiplexer_2 (.in0(\时钟 ), .in1(\时钟2 ), .out(multiplexer_2_out), .sel(in_2));
  Multiplexer #(.width(16), .enable("false")) multiplexer_3 (
    .in0(multiplexer_4_out), .in1(in_1), .out(multiplexer_3_out), .sel(in_2));
  Hex_Digit_Display hex_digit_display_1 (.value(\_1寄存器数据 [15:12]));  // open: dp
  Hex_Digit_Display hex_digit_display_2 (.value(\_1寄存器数据 [11:8]));  // open: dp
  Hex_Digit_Display hex_digit_display_3 (.value(\_1寄存器数据 [7:4]));  // open: dp
  Hex_Digit_Display hex_digit_display_4 (.value(\_1寄存器数据 [3:0]));  // open: dp
  \寄存器组  \u_寄存器组_1  (
    .\写入的数据 (multiplexer_3_out), .\读写信号 (\读写信号 ), .\A的选择输出 (\读出选择1 ), .\选择寄存器信号 (multiplexer_1_out),
    .\B的选择输出 (\读出选择2 ), .\时钟信号 (multiplexer_2_out), .\A输出 (\寄存器组_1_a输出 ), .\B输出 (\寄存器组_1_b输出 ),
    .\_1号寄存器输出 (\_1寄存器数据 ), .\_2号寄存器输出 (\_2寄存器数据 ), .\_3号寄存器输出 (\_3寄存器数据 ), .\_4号寄存器输出 (\_4寄存器数据 ));
  Hex_Digit_Display hex_digit_display_5 (.value(\_2寄存器数据 [15:12]));  // open: dp
  Hex_Digit_Display hex_digit_display_6 (.value(\_2寄存器数据 [11:8]));  // open: dp
  Hex_Digit_Display hex_digit_display_7 (.value(\_2寄存器数据 [7:4]));  // open: dp
  Clock clock_2 (.out(\时钟 ));
  Hex_Digit_Display hex_digit_display_8 (.value(\_2寄存器数据 [3:0]));  // open: dp
  Hex_Digit_Display hex_digit_display_9 (.value(\_3寄存器数据 [15:12]));  // open: dp
  Hex_Digit_Display hex_digit_display_10 (.value(\_3寄存器数据 [7:4]));  // open: dp
  Hex_Digit_Display hex_digit_display_11 (.value(\_3寄存器数据 [11:8]));  // open: dp
  \立即数扩展  \u_立即数扩展_1  (.\输入的数据 ({\jump数 [7:3], func}), .\扩展后的数 (\立即数扩展_1_扩展后的数 ), .\选择扩展方式 (\立即数扩展方式 ));
  Multiplexer #(.width(16), .enable("false")) multiplexer_4 (
    .in0(\存储器数据 ), .in1(multiplexer_7_out), .out(multiplexer_4_out), .sel(\写入寄存器数据2 ));
  Hex_Digit_Display hex_digit_display_12 (.value(\_3寄存器数据 [3:0]));  // open: dp
  Multiplexer #(.width(16), .enable("false")) multiplexer_5 (
    .in0(\寄存器组_1_a输出 ), .in1(\立即数扩展_1_扩展后的数 ), .out(multiplexer_5_out), .sel(\ALU_X输入选择 ));
  Hex_Digit_Display hex_digit_display_13 (.value(\ALU计算方式 ));  // open: dp
  Multiplexer #(.select(2), .width(16), .enable("false")) multiplexer_6 (
    .in0(\寄存器组_1_b输出 ), .in1(\立即数扩展_1_扩展后的数 ), .in2(16'h8), .out(multiplexer_6_out), .sel(\ALU_Y输入选择 ));  // open: in3
  Multiplexer #(.width(16), .enable("false")) multiplexer_7 (
    .in0(\n16位alu_1_p5 ), .in1(bit_extender_1_out), .out(multiplexer_7_out), .sel(\写入寄存器数据1 ));
  assign bit_extender_1_out = {{15{1'b0}}, multiplexer_8_out};  // Bit_Extender bit_extender_1
  // _16位ALU 16位alu_1: pin names not known; wires that end beside it: \ALU计算方式 , multiplexer_5_out, multiplexer_6_out, \符号位 , \n16位alu_1_p5 , \n16位alu_1_p6 
  Multiplexer #(.enable("false")) multiplexer_8 (.in0(1'b0), .in1(1'b1), .out(multiplexer_8_out), .sel(\符号位 ));
  \下地址处理  \u_下地址处理_1  (
    .\PC输入 (counter_1_q), .\offset立即数输入 ({\jump数 [7:3], func}), .\jump地址数输入 ({\jump数 , func}),
    .\_0判断输入 (\n16位alu_1_p6 ), .\下条指令地址 (\下地址处理_1_下条指令地址 ), .\bep相等 (\beq相等 ), .\bne不相等 (\bne不相等 ),
    .\bgt大于 (\bgt大于 ), .\符号位输入 (\符号位 ), .\jump指令输入 (\jump指令输入 ));
  RAM #(.addrWidth(16), .dataWidth(16), .bus("separate")) ram_1 (
    .addr(\n16位alu_1_p5 ), .din(\寄存器组_1_b输出 ), .data(\存储器数据 ), .str(\RAM存储 ), .clk(\时钟 ), .ld(\RAM输出 ),
    .clr(\RAM清空 ));  // open: sel
  Counter #(.width(16), .max('hffff)) counter_1 (
    .load(\计数器加载端 ), .D(\下地址处理_1_下条指令地址 ), .count(\计数器计数端 ), .Q(counter_1_q), .clk(\时钟 ));  // open: carry, clr
  ROM #(.addrWidth(16), .dataWidth(16)) rom_1 (.addr(counter_1_q), .data({\op码 , \jump数 , func}));  // open: sel
  \主译码器  \u_主译码器_1  (
    .func(func), .op4(\op码 [3]), .op3(\op码 [2]), .op2(\op码 [1]), .op1(\op码 [0]), .\读写信号 (\读写信号_t ),
    .\写入寄存器数据1 (\写入寄存器数据1 ), .\写入寄存器数据2 (\写入寄存器数据2 ), .s3(S3), .s2(\ALU计算方式 [2]), .s1(\ALU计算方式 [1]),
    .s0(\ALU计算方式 [0]), .\立即数扩展方式 (\立即数扩展方式_t ), .\ALU_X输入选择 (\ALU_X输入选择_t ), .\ALU_Y输入选择1 (\ALU_Y输入选择 [1]),
    .\ALU_Y输入选择2 (\ALU_Y输入选择 [0]), .\RAM存储 (\RAM存储_t ), .\RAM输出 (\RAM输出_t ), .\计数器计数端 (\计数器计数端_t ),
    .\计数器加载端 (\计数器加载端_t ), .\beq相等 (\beq相等 ), .\bne不相等 (\bne不相等 ), .\bgt大于 (\bgt大于 ),
    .\jump指令输入 (\jump指令输入 ), .\读出选择1_1 (\读出选择1 [1]), .\读出选择1_2 (\读出选择1 [0]), .\读出选择2_1 (\读出选择2 [1]),
    .\读出选择2_2 (\读出选择2 [0]), .\选择寄存器信号_1 (\选择寄存器信号 [1]), .\选择寄存器信号_2 (\选择寄存器信号 [0]));

  // Other names for the same wires on the sheet: ALU_Y输入选择2 = \ALU_Y输入选择 [0]; S0 = \ALU计算方式 [0]; S1 = \ALU计算方式 [1];
  //   S2 = \ALU计算方式 [2]; S3_t = \ALU计算方式 [3]; jump数[2:0] = func; 立即数[7:0] = {\jump数 [7:3], func};
  //   寄存器3[1:0] = \jump数 [7:6]; sta寄存器选择[1:0] = in_3; 初始化数据[15:0] = in_1; 寄存器1[1:0] = \jump数 [11:10];
  //   寄存器2[1:0] = \jump数 [9:8]; 读出选择1_2 = \读出选择1 [0]; 读出选择1_1 = \读出选择1 [1]; 读出选择2_2 = \读出选择2 [0];
  //   读出选择2_1 = \读出选择2 [1]; 选 = in_2; 选择寄存器信号_2 = \选择寄存器信号 [0]; 选择寄存器信号_1 = \选择寄存器信号 [1]

  // Notes on the sheet:
  //   contents of rom_1 (hex, n*v repeats v):
  //   180 181 182 183 184 185 186 187 1163 2163 3163 4193 5193 6193 7101 8101 9101 a010 b000
endmodule

module \寄存器组  (
  input  [15:0] \写入的数据 ,
  input  \读写信号 ,
  input  [1:0] \A的选择输出 ,
  input  [1:0] \选择寄存器信号 ,
  input  [1:0] \B的选择输出 ,
  input  \时钟信号 ,
  output [15:0] \A输出 ,
  output [15:0] \B输出 ,
  output [15:0] \_1号寄存器输出 ,
  output [15:0] \_2号寄存器输出 ,
  output [15:0] \_3号寄存器输出 ,
  output [15:0] \_4号寄存器输出 
);

  wire and_1_out, and_2_out, and_3_out, and_4_out, decoder_1_out0, decoder_1_out1, decoder_1_out2,
       decoder_1_out3;

  Decoder #(.select(2)) decoder_1 (
    .out0(decoder_1_out0), .out1(decoder_1_out1), .out2(decoder_1_out2), .out3(decoder_1_out3),
    .sel(\选择寄存器信号 ));  // open: en
  and and_1 (and_1_out, decoder_1_out0, \读写信号 );
  and and_2 (and_2_out, decoder_1_out1, \读写信号 );
  and and_3 (and_3_out, decoder_1_out2, \读写信号 );
  and and_4 (and_4_out, decoder_1_out3, \读写信号 );
  Register #(.width(16)) register_1 (.D(\写入的数据 ), .en(and_1_out), .Q(\_1号寄存器输出 ), .clk(\时钟信号 ));  // open: clr
  Register #(.width(16)) register_2 (.D(\写入的数据 ), .en(and_2_out), .Q(\_2号寄存器输出 ), .clk(\时钟信号 ));  // open: clr
  Register #(.width(16)) register_3 (.D(\写入的数据 ), .en(and_3_out), .Q(\_3号寄存器输出 ), .clk(\时钟信号 ));  // open: clr
  Register #(.width(16)) register_4 (.D(\写入的数据 ), .en(and_4_out), .Q(\_4号寄存器输出 ), .clk(\时钟信号 ));  // open: clr
  Multiplexer #(.select(2), .width(16)) multiplexer_1 (
    .in0(\_1号寄存器输出 ), .in1(\_2号寄存器输出 ), .in2(\_3号寄存器输出 ), .in3(\_4号寄存器输出 ), .out(\A输出 ), .sel(\A的选择输出 ));  // open: en
  Multiplexer #(.select(2), .width(16)) multiplexer_2 (
    .in0(\_1号寄存器输出 ), .in1(\_2号寄存器输出 ), .in2(\_3号寄存器输出 ), .in3(\_4号寄存器输出 ), .out(\B输出 ), .sel(\B的选择输出 ));  // open: en
endmodule

module \下地址处理  (
  input  [15:0] \PC输入 ,
  input  [7:0] \offset立即数输入 ,
  input  [11:0] \jump地址数输入 ,
  input  \jump指令输入 ,
  input  \bep相等 ,
  input  \bne不相等 ,
  input  \bgt大于 ,
  input  \_0判断输入 ,
  input  \符号位输入 ,
  output [15:0] \下条指令地址 
);

  wire and_2_out, and_3_out, and_4_out, not_1_out, not_2_out, or_2_out;
  wire [15:0] adder_1_out, adder_2_out, and_1_out, bit_extender_1_out, bit_extender_2_out, multiplexer_1_out,
       or_1_out;

  assign bit_extender_1_out = {{8{1'b0}}, \offset立即数输入 };  // Bit_Extender bit_extender_1
  assign bit_extender_2_out = {{4{1'b0}}, \jump地址数输入 };  // Bit_Extender bit_extender_2
  Adder #(.width(16)) adder_1 (.a(\PC输入 ), .b(16'h1), .out(adder_1_out));  // open: cin, cout
  assign and_1_out = adder_1_out & 16'hf000;  // AND_Gate and_1, 16 bits wide
  Adder #(.width(16)) adder_2 (.a(adder_1_out), .b(bit_extender_1_out), .out(adder_2_out));  // open: cin, cout
  assign or_1_out = and_1_out | bit_extender_2_out;  // OR_Gate or_1, 16 bits wide
  and and_2 (and_2_out, \bep相等 , \_0判断输入 );
  or or_2 (or_2_out, and_2_out, and_3_out, and_4_out);
  and and_3 (and_3_out, \bne不相等 , not_1_out);
  Multiplexer #(.width(16), .enable("false")) multiplexer_1 (
    .in0(adder_1_out), .in1(adder_2_out), .out(multiplexer_1_out), .sel(or_2_out));
  not not_1 (not_1_out, \_0判断输入 );
  and and_4 (and_4_out, \bgt大于 , not_2_out);
  not not_2 (not_2_out, \符号位输入 );
  Multiplexer #(.width(16), .enable("false")) multiplexer_2 (
    .in0(multiplexer_1_out), .in1(or_1_out), .out(\下条指令地址 ), .sel(\jump指令输入 ));
endmodule

// 扩展
module \立即数扩展  (
  input  [7:0] \输入的数据 ,
  input  \选择扩展方式 ,
  output [15:0] \扩展后的数 
);

  wire [15:0] bit_extender_1_out, bit_extender_2_out;

  assign bit_extender_1_out = {{8{1'b0}}, \输入的数据 };  // Bit_Extender bit_extender_1
  assign bit_extender_2_out = {{8{\输入的数据 [7]}}, \输入的数据 };  // Bit_Extender bit_extender_2
  Multiplexer #(.width(16), .enable("false")) multiplexer_1 (
    .in0(bit_extender_1_out), .in1(bit_extender_2_out), .out(\扩展后的数 ), .sel(\选择扩展方式 ));
endmodule

module \译码器1  (
  input  op4,
  input  op3,
  input  op2,
  input  op1,
  output \读写信号 ,
  output \写入寄存器数据1 ,
  output \写入寄存器数据2 ,
  output s3,
  output s2,
  output s1,
  output s0,
  output \立即数扩展方式 ,
  output \ALU_X输入选择 ,
  output \ALU_Y输入选择1 ,
  output \ALU_Y输入选择2 ,
  output \RAM存储 
);

  wire and_1_out, and_2_out, and_3_out, and_4_out, and_6_out, and_7_out, and_8_out, and_9_out, and_10_out,
       and_11_out, and_12_out, and_13_out, and_14_out, and_15_out, and_16_out, and_17_out, and_18_out,
       and_21_out, and_22_out, and_23_out, and_24_out, not_1_out, not_2_out, not_3_out, not_4_out, not_5_out,
       not_6_out, not_7_out, not_8_out, not_9_out, not_10_out, not_11_out, not_12_out, not_13_out,
       not_14_out, not_15_out, not_16_out, not_17_out, not_18_out, not_19_out, not_20_out, not_21_out,
       not_22_out, not_23_out, not_24_out, not_25_out, not_26_out, not_27_out, not_28_out, not_29_out,
       not_30_out, not_31_out;

  not not_1 (not_1_out, op4);
  and and_1 (and_1_out, not_1_out, not_2_out);
  not not_2 (not_2_out, op3);
  not not_3 (not_3_out, op4);
  and and_2 (and_2_out, not_3_out, not_4_out);
  not not_4 (not_4_out, op2);
  not not_5 (not_5_out, op3);
  and and_3 (and_3_out, not_5_out, op2, op1);
  and and_4 (and_4_out, op4, op3);
  and and_5 (\写入寄存器数据1 , op4, op3);
  not not_6 (not_6_out, op3);
  not not_7 (not_7_out, op1);
  and and_6 (and_6_out, op4, op2, op1);
  and and_7 (and_7_out, op4, op3);
  not not_8 (not_8_out, op4);
  not not_9 (not_9_out, op3);
  not not_10 (not_10_out, op2);
  not not_11 (not_11_out, op4);
  not not_12 (not_12_out, op3);
  and and_8 (and_8_out, not_11_out, not_12_out, op1);
  not not_13 (not_13_out, op4);
  not not_14 (not_14_out, op3);
  and and_9 (and_9_out, not_13_out, not_14_out, op2);
  not not_15 (not_15_out, op3);
  and and_10 (and_10_out, not_15_out, op2, not_16_out);
  not not_16 (not_16_out, op1);
  and and_11 (and_11_out, op3, op2, op1);
  and and_12 (and_12_out, op4, not_17_out);
  not not_17 (not_17_out, op2);
  and and_13 (and_13_out, op4, not_18_out);
  not not_18 (not_18_out, op1);
  not not_19 (not_19_out, op2);
  and and_14 (and_14_out, not_19_out, not_20_out);
  not not_20 (not_20_out, op1);
  not not_21 (not_21_out, op4);
  not not_22 (not_22_out, op3);
  not not_23 (not_23_out, op2);
  not not_24 (not_24_out, op4);
  not not_25 (not_25_out, op3);
  not not_26 (not_26_out, op2);
  not not_27 (not_27_out, op4);
  not not_28 (not_28_out, op3);
  and and_15 (and_15_out, not_27_out, not_28_out, op2);
  and and_16 (and_16_out, op3, not_29_out);
  not not_29 (not_29_out, op2);
  and and_17 (and_17_out, op3, not_30_out);
  not not_30 (not_30_out, op1);
  and and_18 (and_18_out, op4, op3);
  and and_19 (\RAM存储 , op3, op2, not_31_out);
  not not_31 (not_31_out, op1);
  or or_1 (\读写信号 , and_1_out, and_2_out, and_3_out, and_4_out);
  or or_2 (\写入寄存器数据2 , not_6_out, not_7_out, op2, op4);
  or or_3 (s3, and_6_out, and_7_out);
  and and_20 (s2, not_8_out, not_9_out, not_10_out, op1);
  or or_4 (s1, and_8_out, and_9_out);
  or or_5 (s0, and_10_out, and_11_out, and_12_out, and_13_out);
  or or_6 (\立即数扩展方式 , and_14_out, op3, op4);
  and and_21 (and_21_out, not_21_out, not_22_out, not_23_out, op1);
  or or_7 (\ALU_X输入选择 , and_21_out, and_22_out);
  and and_22 (and_22_out, op4, op3);
  and and_23 (and_23_out, not_24_out, not_25_out, not_26_out, op1);
  or or_8 (\ALU_Y输入选择1 , and_23_out, and_24_out);
  and and_24 (and_24_out, op4, op3);
  or or_9 (\ALU_Y输入选择2 , and_15_out, and_16_out, and_17_out, and_18_out);
endmodule

module \译码器2  (
  input  op4,
  input  op3,
  input  op2,
  input  op1,
  output \RAM输出 ,
  output \计数器计数端 ,
  output \计数器加载端 ,
  output \beq相等 ,
  output \bne不相等 ,
  output \bgt大于 ,
  output \jump指令输入 
);

  wire and_1_out, and_2_out, and_3_out, and_4_out, and_5_out, and_6_out, and_7_out, and_8_out, and_9_out,
       and_10_out, and_11_out, and_12_out, and_13_out, and_14_out, and_15_out, and_16_out, not_1_out,
       not_2_out, not_3_out, not_4_out, not_5_out, not_6_out, not_7_out, not_8_out, not_9_out, not_10_out,
       not_11_out;

  not not_1 (not_1_out, op2);
  and and_1 (and_1_out, op3, not_1_out, op1);
  and and_2 (and_2_out, op4, op3);
  not not_2 (not_2_out, op4);
  and and_3 (and_3_out, not_2_out, not_3_out);
  not not_3 (not_3_out, op3);
  not not_4 (not_4_out, op4);
  and and_4 (and_4_out, not_4_out, not_5_out);
  not not_5 (not_5_out, op2);
  not not_6 (not_6_out, op4);
  and and_5 (and_5_out, not_6_out, not_7_out);
  not not_7 (not_7_out, op1);
  and and_6 (and_6_out, op3, op2, op1);
  and and_7 (and_7_out, op4, not_8_out);
  not not_8 (not_8_out, op2);
  and and_8 (and_8_out, op4, not_9_out);
  not not_9 (not_9_out, op1);
  and and_9 (and_9_out, op3, op2, op1);
  and and_10 (and_10_out, op4, op3);
  and and_11 (and_11_out, op4, not_10_out, not_11_out);
  not not_10 (not_10_out, op2);
  not not_11 (not_11_out, op1);
  and and_12 (and_12_out, op4, op3);
  and and_13 (and_13_out, op4, op1);
  and and_14 (and_14_out, op4, op3);
  and and_15 (and_15_out, op4, op2);
  and and_16 (and_16_out, op4, op3);
  or or_1 (\RAM输出 , and_1_out, and_2_out);
  or or_2 (\计数器计数端 , and_3_out, and_4_out, and_5_out);
  or or_3 (\计数器加载端 , and_6_out, and_7_out, and_8_out);
  or or_4 (\beq相等 , and_9_out, and_10_out);
  or or_5 (\bne不相等 , and_11_out, and_12_out);
  or or_6 (\bgt大于 , and_13_out, and_14_out);
  or or_7 (\jump指令输入 , and_15_out, and_16_out);
endmodule

module \译码器3  (
  input  op4,
  input  op3,
  input  op2,
  input  op1,
  output \读出选择1_1 ,
  output \读出选择1_2 ,
  output \读出选择2_1 ,
  output \读出选择2_2 ,
  output \选择寄存器信号_1 ,
  output \选择寄存器信号_2 
);

  wire and_4_out, and_5_out, not_1_out, not_2_out, not_3_out;

  and and_1 (\读出选择1_1 , op4, op3);
  and and_2 (\读出选择1_2 , op4, op2);
  and and_3 (\读出选择2_1 , op4, op3);
  not not_1 (not_1_out, op3);
  not not_2 (not_2_out, op2);
  and and_4 (and_4_out, not_1_out, not_2_out, not_3_out);
  not not_3 (not_3_out, op1);
  and and_5 (and_5_out, op3, op2);
  or or_1 (\选择寄存器信号_2 , op1, op2, op3);
  or or_2 (\选择寄存器信号_1 , and_4_out, and_5_out);

  assign \读出选择2_2  = 1'b1;
endmodule

module \译码器1_2_3组合  (
  input  op4,
  input  op3,
  input  op2,
  input  op1,
  output \读写信号 ,
  output \写入寄存器数据1 ,
  output \写入寄存器数据2 ,
  output s0,
  output s2,
  output s1,
  output s0_2,
  output \立即数扩展方式 ,
  output \ALU_X输入选择 ,
  output \ALU_Y输入选择1 ,
  output \ALU_Y输入选择2 ,
  output \RAM存储 ,
  output \RAM输出 ,
  output \计数器计数端 ,
  output \计数器加载端 ,
  output \beq相等 ,
  output \bne不相等 ,
  output \bgt大于 ,
  output \jump指令输入 ,
  output \读出选择1_1 ,
  output \读出选择1_2 ,
  output \读出选择2_1 ,
  output \读出选择2_2 ,
  output \选择寄存器信号_1 ,
  output \选择寄存器信号_2 
);

  \译码器1  \u_译码器1_1  (
    .op4(op4), .op3(op3), .op2(op2), .op1(op1), .\读写信号 (\读写信号 ), .\写入寄存器数据1 (\写入寄存器数据1 ),
    .\写入寄存器数据2 (\写入寄存器数据2 ), .s3(s0), .s2(s2), .s1(s1), .s0(s0_2), .\立即数扩展方式 (\立即数扩展方式 ),
    .\ALU_X输入选择 (\ALU_X输入选择 ), .\ALU_Y输入选择1 (\ALU_Y输入选择1 ), .\ALU_Y输入选择2 (\ALU_Y输入选择2 ), .\RAM存储 (\RAM存储 ));
  \译码器2  \u_译码器2_1  (
    .op4(op4), .op3(op3), .op2(op2), .op1(op1), .\RAM输出 (\RAM输出 ), .\计数器计数端 (\计数器计数端 ), .\计数器加载端 (\计数器加载端 ),
    .\beq相等 (\beq相等 ), .\bne不相等 (\bne不相等 ), .\bgt大于 (\bgt大于 ), .\jump指令输入 (\jump指令输入 ));
  \译码器3  \u_译码器3_1  (
    .op4(op4), .op3(op3), .op2(op2), .op1(op1), .\读出选择1_1 (\读出选择1_1 ), .\读出选择1_2 (\读出选择1_2 ),
    .\读出选择2_1 (\读出选择2_1 ), .\读出选择2_2 (\读出选择2_2 ), .\选择寄存器信号_1 (\选择寄存器信号_1 ), .\选择寄存器信号_2 (\选择寄存器信号_2 ));
endmodule

module \func译码  (
  input  func3,
  input  func2,
  input  func1,
  output \写入寄存器数据1 ,
  output s3,
  output s2,
  output s1,
  output s0
);

  wire and_4_out, and_5_out, and_6_out, not_1_out, not_2_out, not_4_out, not_5_out, not_6_out;

  and and_1 (\写入寄存器数据1 , func1, func2, func3);
  not not_1 (not_1_out, func3);
  not not_2 (not_2_out, func2);
  not not_3 (s1, func2);
  not not_4 (not_4_out, func1);
  not not_5 (not_5_out, func2);
  not not_6 (not_6_out, func3);
  and and_2 (s3, func1, func2, not_1_out);
  and and_3 (s2, func1, not_2_out);
  and and_4 (and_4_out, not_4_out, not_5_out, not_6_out);
  and and_5 (and_5_out, func2, func3);
  and and_6 (and_6_out, func1, func3);
  or or_1 (s0, and_4_out, and_5_out, and_6_out);
endmodule

// 译码器
module \主译码器  (
  input  [2:0] func,
  input  op4,
  input  op3,
  input  op2,
  input  op1,
  output \读写信号 ,
  output \写入寄存器数据1 ,
  output \写入寄存器数据2 ,
  output s3,
  output s2,
  output s1,
  output s0,
  output \立即数扩展方式 ,
  output \ALU_X输入选择 ,
  output \ALU_Y输入选择1 ,
  output \ALU_Y输入选择2 ,
  output \RAM存储 ,
  output \RAM输出 ,
  output \计数器计数端 ,
  output \计数器加载端 ,
  output \beq相等 ,
  output \bne不相等 ,
  output \bgt大于 ,
  output \jump指令输入 ,
  output \读出选择1_1 ,
  output \读出选择1_2 ,
  output \读出选择2_1 ,
  output \读出选择2_2 ,
  output \选择寄存器信号_1 ,
  output \选择寄存器信号_2 
);

  wire comparator_1_eq, comparator_2_eq, comparator_3_eq, comparator_4_eq, s0_t, s1_t, s2_t, s3_t,
       \写入寄存器数据1_t , \译码器1_2_3组合_1_s0 , \译码器1_2_3组合_1_s0_2 , \译码器1_2_3组合_1_s1 , \译码器1_2_3组合_1_s2 ,
       \译码器1_2_3组合_1_写入寄存器数据1 , \选择 ;

  Comparator #(.width(1), .mode("unsigned")) comparator_1 (.a(1'b0), .b(op4), .eq(comparator_1_eq));  // open: gt, lt
  Comparator #(.width(1), .mode("unsigned")) comparator_2 (.a(1'b0), .b(op3), .eq(comparator_2_eq));  // open: gt, lt
  Comparator #(.width(1), .mode("unsigned")) comparator_3 (.a(1'b0), .b(op2), .eq(comparator_3_eq));  // open: gt, lt
  Comparator #(.width(1), .mode("unsigned")) comparator_4 (.a(1'b0), .b(op1), .eq(comparator_4_eq));  // open: gt, lt
  \译码器1_2_3组合  \u_译码器1_2_3组合_1  (
    .op4(op4), .op3(op3), .op2(op2), .op1(op1), .\读写信号 (\读写信号 ), .\写入寄存器数据1 (\译码器1_2_3组合_1_写入寄存器数据1 ),
    .\写入寄存器数据2 (\写入寄存器数据2 ), .s0(\译码器1_2_3组合_1_s0 ), .s2(\译码器1_2_3组合_1_s2 ), .s1(\译码器1_2_3组合_1_s1 ),
    .s0_2(\译码器1_2_3组合_1_s0_2 ), .\立即数扩展方式 (\立即数扩展方式 ), .\ALU_X输入选择 (\ALU_X输入选择 ),
    .\ALU_Y输入选择1 (\ALU_Y输入选择1 ), .\ALU_Y输入选择2 (\ALU_Y输入选择2 ), .\RAM存储 (\RAM存储 ), .\RAM输出 (\RAM输出 ),
    .\计数器计数端 (\计数器计数端 ), .\计数器加载端 (\计数器加载端 ), .\beq相等 (\beq相等 ), .\bne不相等 (\bne不相等 ), .\bgt大于 (\bgt大于 ),
    .\jump指令输入 (\jump指令输入 ), .\读出选择1_1 (\读出选择1_1 ), .\读出选择1_2 (\读出选择1_2 ), .\读出选择2_1 (\读出选择2_1 ),
    .\读出选择2_2 (\读出选择2_2 ), .\选择寄存器信号_1 (\选择寄存器信号_1 ), .\选择寄存器信号_2 (\选择寄存器信号_2 ));
  and and_1 (\选择 , comparator_1_eq, comparator_2_eq, comparator_3_eq, comparator_4_eq);
  Multiplexer #(.enable("false")) multiplexer_1 (
    .in0(\译码器1_2_3组合_1_写入寄存器数据1 ), .in1(\写入寄存器数据1_t ), .out(\写入寄存器数据1 ), .sel(\选择 ));
  Multiplexer #(.enable("false")) multiplexer_2 (.in0(\译码器1_2_3组合_1_s0 ), .in1(s3_t), .out(s3), .sel(\选择 ));
  Multiplexer #(.enable("false")) multiplexer_3 (.in0(\译码器1_2_3组合_1_s2 ), .in1(s2_t), .out(s2), .sel(\选择 ));
  Multiplexer #(.enable("false")) multiplexer_4 (.in0(\译码器1_2_3组合_1_s1 ), .in1(s1_t), .out(s1), .sel(\选择 ));
  Multiplexer #(.enable("false")) multiplexer_5 (.in0(\译码器1_2_3组合_1_s0_2 ), .in1(s0_t), .out(s0), .sel(\选择 ));
  \func译码  \func译码_1  (
    .func3(func[0]), .func2(func[1]), .func1(func[2]), .\写入寄存器数据1 (\写入寄存器数据1_t ), .s3(s3_t), .s2(s2_t),
    .s1(s1_t), .s0(s0_t));
endmodule
